# Fritzing sketch bathbuddy (saved by Fritzing 0.9.9b)
breadboards: 1

parts:
  S1 = Momentary Switch [package=ksa_sealed_tac_switch]
  S2 = Momentary Switch [package=ksa_sealed_tac_switch]
  M1 = RioRand LM2596
  VCC1 = 4 x AAA Battery Mount
  S3 = Momentary Switch [package=ksa_sealed_tac_switch]
  U1 = ESP8266-01S [part_number=ESP8266]

nets:
  N1: S1.1, U1.TXD
  N2: S1.4, S2.2, M1.Pin_4, S3.4, U1.GND
  N3: S2.3, U1.GPIO_2
  N4: M1.Pin_1, VCC1.+
  N5: M1.Pin_2, VCC1.-
  N6: M1.Pin_3, U1.VCC, U1.CH_PD
  N7: S3.1, U1.RXD
